# Fritzing sketch robotics (saved by Fritzing 0.9.3b)

parts:
  Part1 = Arduino Mega ADK (Rev3)
  SERVO1 = Tower Pro SG90 servo [part_number=101246]
  SERVO2 = Tower Pro SG90 servo [part_number=101246]
  JACK1 = 2.1mm Barrel Jack with Terminal Block
  J1 = Basic Servo
  J2 = Basic Servo
  J3 = Basic Servo

nets:
  GND: Part1.GND, SERVO1.GND, SERVO2.GND, JACK1.NEG, J1.gnd, J2.gnd, J3.gnd
  VCC: Part1.VIN, SERVO1.+5V, SERVO2.+5V, JACK1.POS, J1.vcc, J2.vcc, J3.vcc
  N1: Part1.D2_PWM, SERVO2.Signal
  N2: Part1.D3_PWM, SERVO1.Signal
  N3: Part1.D4_PWM, J1.pulse
  N4: Part1.D5_PWM, J3.pulse
  N5: Part1.D6_PWM, J2.pulse

notes:
  5V Power Supply

custom parts:
  Tower Pro SG90 servo: Original file by John De Cristofaro http://www.adafruit.com/products/1449 Adafruit Feedback Servo (Small) Edited by: e-radionica.com 28/9/2015
